// Logisim project Address Decode.circ as structural Verilog: 1 circuit, main circuit main
module main (
  input  [7:0] Bank,
  input  VPB,
  input  in_3,
  input  in_4,
  input  in_5,
  input  in_6,
  input  in_7,
  input  in_8,
  input  in_9,
  input  in_10,
  input  in_11,
  input  in_12,
  input  in_13,
  input  in_14,
  input  in_15,
  input  in_16,
  input  in_17,
  input  in_18,
  input  in_19
);

  wire and_1_out, clock_1_out, IRQB_out, not_1_out, or_1_out, pull_resistor_5_node, pull_resistor_6_node,
       undriven, undriven_2, undriven_3, undriven_4;
  wire [2:0] priority_encoder_1_out, priority_encoder_2_out;
  wire [3:0] controlled_buffer_1_out;
  wire [3:3] pull_resistor_1_node, pull_resistor_2_node;
  wire [7:0] pull_resistor_4_node, ram_1_data, register_1_q;
  wire [15:0] multiplexer_1_out;

  Clock clock_1 (.out(clock_1_out));
  Pull_Resistor pull_resistor_1 (.node(pull_resistor_1_node[3]));
  // Probe on priority_encoder_1_out
  Priority_Encoder #(.disabled(0)) priority_encoder_1 (
    .in0(in_4), .in1(in_5), .in2(in_6), .in3(in_7), .in4(in_8), .in5(in_9), .in6(in_10), .in7(in_11),
    .out(priority_encoder_1_out), .en_in(in_3));
  assign controlled_buffer_1_out = not_1_out ? {pull_resistor_1_node[3], priority_encoder_1_out} : 4'bz;  // Controlled_Buffer controlled_buffer_1
  not IRQB (IRQB_out, and_1_out);
  and and_1 (and_1_out, undriven_2, undriven_3);
  not not_1 (not_1_out, undriven_4);
  Pull_Resistor #(.pull(1)) pull_resistor_2 (.node(pull_resistor_2_node[3]));
  Pull_Resistor #(.pull(1)) pull_resistor_3 (.node(priority_encoder_2_out[2]));
  Priority_Encoder #(.disabled(0)) priority_encoder_2 (
    .in0(in_12), .in1(in_13), .in2(in_14), .in3(in_15), .in4(in_16), .in5(in_17), .in6(in_18), .in7(in_19),
    .out(priority_encoder_2_out), .en_in(in_3));
  assign controlled_buffer_1_out = undriven_4 ? {pull_resistor_2_node[3], priority_encoder_2_out} : 4'bz;  // Controlled_Buffer controlled_buffer_2
  // Probe on priority_encoder_2_out
  // Probe on {{3{pull_resistor_1_node[3]}}, controlled_buffer_1_out, pull_resistor_1_node[3]}
  Register #(.trigger("high")) register_1 (
    .D({{3{pull_resistor_1_node[3]}}, controlled_buffer_1_out, pull_resistor_1_node[3]}), .Q(register_1_q),
    .clk(or_1_out));  // open: en, clr
  or or_1 (or_1_out, undriven, undriven_4);
  Pull_Resistor #(.pull(1)) pull_resistor_4 (.node(pull_resistor_4_node));
  // Probe on 16'h10ab
  Pull_Resistor #(.pull(1)) pull_resistor_5 (.node(pull_resistor_5_node));
  // Probe on {pull_resistor_4_node, register_1_q}
  // Probe on multiplexer_1_out
  Multiplexer #(.width(16)) multiplexer_1 (
    .in0(16'h10ab), .in1({pull_resistor_4_node, register_1_q}), .out(multiplexer_1_out), .sel(IRQB_out),
    .en(pull_resistor_5_node));
  Pull_Resistor #(.pull(1)) pull_resistor_6 (.node(pull_resistor_6_node));
  RAM #(.addrWidth(16)) ram_1 (
    .addr(multiplexer_1_out), .data(ram_1_data), .sel(pull_resistor_6_node));  // open: clk, ld, clr
endmodule
