// Logisim project Test.circ as structural Verilog: 1 circuit, main circuit main
module main (
);

  wire clock_1_out, clock_2_out, clock_3_out, lvc573_1_p2, lvc573_1_p4, lvc16373_1_p2, lvc16373_1_p7,
       lvc16373_1_p8, not_1_out;
  wire [3:0] counter_1_q, counter_2_q;

  Random random_1 ();  // open: clk, next, out, clr
  Clock clock_1 (.out(clock_1_out));
  Random random_2 ();  // open: clk, next, out, clr
  Clock clock_2 (.out(clock_2_out));
  Clock clock_3 (.out(clock_3_out));
  Counter #(.max('hf), .width(4)) counter_1 (
    .Q(counter_1_q), .clk(clock_1_out));  // open: load, D, count, carry, up, clr
  Counter #(.max('hf), .width(4)) counter_2 (
    .Q(counter_2_q), .clk(clock_2_out));  // open: load, D, count, carry, up, clr
  // LVC4245 lvc4245_1: pin names not known
  // DS1813 ds1813_1: pin names not known
  // LVC16373 lvc16373_1: pin names not known; wires that end beside it: counter_1_q[0], lvc16373_1_p2, counter_1_q[2], counter_1_q[1], lvc16373_1_p2, counter_1_q[3], lvc16373_1_p7, lvc16373_1_p8
  // LVC573 lvc573_1: pin names not known; wires that end beside it: counter_2_q[0], lvc573_1_p2, counter_2_q[2], lvc573_1_p4
  not not_1 (not_1_out, clock_3_out);
  // LVC543 lvc543_1: pin names not known; wires that end beside it: clock_3_out, not_1_out
  // Probe on lvc16373_1_p7
  // Probe on lvc16373_1_p8
  // Probe on lvc573_1_p4
  // W65C816 w65c816_1: pin names not known
  // W65C02S w65c02s_1: pin names not known
endmodule
