// Logisim project demo.circ as structural Verilog: 1 circuit, main circuit main
module main (
);

  wire Abort_out, and_1_out, and_2_out, clock_1_out, IRQ_out, NMI_out, not_1_out, not_2_out, not_3_out,
       not_4_out, not_5_out, not_6_out, pull_resistor_2_node, Reset_out, w65c816s_1_p1, w65c816s_1_p2,
       w65c816s_1_p3, w65c816s_1_p14, w65c816s_1_p15, w65c816s_1_p16, w65c816s_1_p17, w65c816s_1_p18,
       w65c816s_1_p19;
  wire [7:0] controlled_buffer_2_out, w65c816s_1_p13;
  wire [15:0] w65c816s_1_p12;

  Clock clock_1 (.out(clock_1_out));
  Button Abort (.out(Abort_out));
  Button IRQ (.out(IRQ_out));
  Button NMI (.out(NMI_out));
  Button Reset (.out(Reset_out));
  not not_1 (not_1_out, Abort_out);
  not not_2 (not_2_out, IRQ_out);
  not not_3 (not_3_out, NMI_out);
  not not_4 (not_4_out, Reset_out);
  // W65C816S w65c816s_1: pin names not known; wires that end beside it: w65c816s_1_p1, w65c816s_1_p2, w65c816s_1_p3, not_1_out, not_2_out, not_3_out, not_4_out, clock_1_out, w65c816s_1_p1, w65c816s_1_p2, w65c816s_1_p3, w65c816s_1_p12, w65c816s_1_p13, w65c816s_1_p14, w65c816s_1_p15, w65c816s_1_p16, w65c816s_1_p17, w65c816s_1_p18, w65c816s_1_p19, w65c816s_1_p16, w65c816s_1_p17, w65c816s_1_p18, w65c816s_1_p19
  Register #(.trigger("high")) register_1 (.D(w65c816s_1_p13), .clk(clock_1_out));  // open: en, Q, clr
  not not_5 (not_5_out, clock_1_out);
  // Probe on w65c816s_1_p13
  Pull_Resistor #(.pull(1)) pull_resistor_1 (.node(w65c816s_1_p15));
  assign w65c816s_1_p13 = and_1_out ? controlled_buffer_2_out : 8'bz;  // Controlled_Buffer controlled_buffer_1
  and and_1 (and_1_out, w65c816s_1_p14, not_5_out);
  not not_6 (not_6_out, w65c816s_1_p14);
  assign controlled_buffer_2_out = and_2_out ? w65c816s_1_p13 : 8'bz;  // Controlled_Buffer controlled_buffer_2
  and and_2 (and_2_out, not_5_out, not_6_out);
  RAM #(.addrWidth(16), .databus("bidir"), .enables("line"), .trigger("high"), .\type ("nonvolatile")) ram_1 (
    .addr(w65c816s_1_p12), .data(controlled_buffer_2_out));  // open: we, oe, clk
  Pull_Resistor #(.pull(1)) pull_resistor_2 (.node(pull_resistor_2_node));
  // Probe on controlled_buffer_2_out
endmodule
