// Logisim project demo2.circ as structural Verilog: 1 circuit, main circuit main
module main (
  input  in_1,
  input  in_2
);

  wire not_1_out;
  wire [7:0] controlled_buffer_1_out, lvc4245_1_p5;

  // Probe on controlled_buffer_1_out
  assign controlled_buffer_1_out = not_1_out ? 8'h43 : 8'bz;  // Controlled_Buffer controlled_buffer_1
  not not_1 (not_1_out, in_2);
  // LVC4245 lvc4245_1: pin names not known; wires that end beside it: controlled_buffer_1_out, in_1, controlled_buffer_1_out, in_2, lvc4245_1_p5, lvc4245_1_p5
  // Probe on lvc4245_1_p5
  assign lvc4245_1_p5 = in_2 ? 8'h3b : 8'bz;  // Controlled_Buffer controlled_buffer_2
endmodule
